# Fritzing sketch hookup (saved by Fritzing 1.0.8)
circuit board: 8.46667cm x 5.64444cm

parts:
  IC1 = AS5600 Magnetic Rotary Encoder Module [package="Breakout Module [THT]"]
  Part1 = Arduino Uno (Rev3)
  J1 = Basic Servo
  Power_plug1 = Power plug

nets:
  VCC: IC1.VCC, Part1.5V
  GND: IC1.GND, Part1.GND, J1.gnd, Power_plug1.GND
  N1: IC1.SCL, Part1.A5/SCL
  N2: IC1.SDA, Part1.A4/SDA
  N3: Part1.A3, J1.pulse

custom parts:
  AS5600 Magnetic Rotary Encoder Module: A breakout module for the ams AS5600 contactless 12-bit magnetic rotary position sensor. Reads the absolute angle of a diametrically-magnetized magnet rotating above the chip, over I2C (SCL/SDA), analog output, or PWM (OUT). VCC accepts 3.3V or 5V depending on the module's onboard regulator; GND is ground. DIR sets the direction of positive rotation (tie to GND or VCC).
